# Fritzing sketch RFID Entrance Guard System (saved by Fritzing 0.8.7b)
breadboards: 1

parts:
  module3 = I2C LCD1602
  元件1 = Arduino Uno (Rev3) - ICSP
  module4 = RFID-RC522
  module5 = relay -v1.0 module

nets:
  N1: module3.SCL, 元件1.A5/SCL
  N2: module3.SDA, 元件1.A4/SDA
  VCC: module3.VCC, 元件1.5V, module5.+
  GND: module3.GND, 元件1.GND, module4.GND, module5.-
  N3: 元件1.D8, module5.S
  N4: 元件1.D2, module4.RST
  N5: 元件1.D3_PWM, module4.MISO
  N6: 元件1.D4, module4.MOSI
  N7: 元件1.D5_PWM, module4.SCK
  N8: 元件1.D6_PWM, module4.NSS
  N9: 元件1.D7, module4.IRQ
  3V3: 元件1.3V3, module4.VCC

notes:
  Relay Module
  RFID Module

custom parts:
  I2C LCD1602: I2C LCD1602 module of SunFounder Sensor Kit
  RFID-RC522: RFID-RC522 module from Sunfounder
  relay -v1.0 module: relay v1.0 module from SunFounder Sensor Kit
