# Fritzing sketch MEGA_BREAD_KEYPAD (saved by Fritzing 0.9.3b)
circuit board: 18.47cm x 15.64cm
breadboards: 3
perfboards: 1

parts:
  Part1 = Arduino Mega 2560 (Rev3)
  VCC1 = Battery block 9V
  R15 = Rotary Potentiometer (Small) [maximum_resistance=100kΩ package=THT]
  R16 = Rotary Potentiometer (Small) [maximum_resistance=100kΩ package=THT]
  LCD1 = LCD screen
  R1C1 = Pushbutton [package="[THT]"]
  R2C1 = Pushbutton [package="[THT]"]
  R3C1 = Pushbutton [package="[THT]"]
  R4C1 = Pushbutton [package="[THT]"]
  R1C2 = Pushbutton [package="[THT]"]
  R2C2 = Pushbutton [package="[THT]"]
  R3C2 = Pushbutton [package="[THT]"]
  R4C2 = Pushbutton [package="[THT]"]
  R1C3 = Pushbutton [package="[THT]"]
  R2C3 = Pushbutton [package="[THT]"]
  R3C3 = Pushbutton [package="[THT]"]
  R4C3 = Pushbutton [package="[THT]"]
  R1C4 = Pushbutton [package="[THT]"]
  R2C4 = Pushbutton [package="[THT]"]
  R3C4 = Pushbutton [package="[THT]"]
  R4C4 = Pushbutton [package="[THT]"]

nets (from the breadboard view):
  N1: Part1.A13, R4C2.Pin_3, R4C2.Pin_4
  N2: Part1.A14, R3C3.Pin_3, R3C3.Pin_4, R4C3.Pin_3, R4C3.Pin_4
  5V: Part1.5V, R15.leg2, R16.leg2, LCD1.VDD
  N3: Part1.GND, VCC1.-
  N4: Part1.VIN, VCC1.+
  N5: Part1.D28, LCD1.RS
  N6: Part1.D29, LCD1.E
  N7: Part1.D30, LCD1.DB0
  N8: Part1.D31, LCD1.DB1
  N9: Part1.D32, LCD1.DB2
  N10: Part1.D33, LCD1.DB3
  N11: Part1.D34, LCD1.DB4
  N12: Part1.D35, LCD1.DB5
  N13: Part1.D36, LCD1.DB6
  N14: Part1.D37, LCD1.DB7
  N15: Part1.D39, R3C1.Pin_1, R3C1.Pin_2
  N16: Part1.D40, R2C1.Pin_1, R2C1.Pin_2, R4C1.Pin_3, R4C1.Pin_4, R2C2.Pin_1, R2C2.Pin_2
  N17: Part1.D41, R1C1.Pin_1, R1C1.Pin_2, R1C2.Pin_1, R1C2.Pin_2, R3C4.Pin_3, R3C4.Pin_4, R4C4.Pin_3, R4C4.Pin_4
  N18: R15.leg1, R16.leg1, LCD1.VSS, LCD1.R/W, LCD1.LED-
  N19: R15.wiper, LCD1.LED+
  N20: R16.wiper, LCD1.V0
  N21: R1C1.Pin_3, R1C1.Pin_4, R2C1.Pin_3, R2C1.Pin_4
  N22: R3C1.Pin_3, R3C1.Pin_4
  N23: R4C1.Pin_1, R4C1.Pin_2
  N24: R1C2.Pin_3, R1C2.Pin_4, R2C2.Pin_3, R2C2.Pin_4, R1C3.Pin_1, R1C3.Pin_2
  N25: R3C2.Pin_1, R3C2.Pin_2
  N26: R3C2.Pin_3, R3C2.Pin_4
  N27: R4C2.Pin_1, R4C2.Pin_2, R4C3.Pin_1, R4C3.Pin_2
  N28: R1C3.Pin_3, R1C3.Pin_4
  N29: R2C3.Pin_1, R2C3.Pin_2
  N30: R2C3.Pin_3, R2C3.Pin_4
  N31: R3C3.Pin_1, R3C3.Pin_2, R3C4.Pin_1, R3C4.Pin_2
  N32: R1C4.Pin_1, R1C4.Pin_2
  N33: R1C4.Pin_3, R1C4.Pin_4, R2C4.Pin_3, R2C4.Pin_4
  N34: R2C4.Pin_1, R2C4.Pin_2
  N35: R4C4.Pin_1, R4C4.Pin_2

// code stored in the sketch: MEGA_BREAD_KEYPAD.ino
#include <LiquidCrystal.h> //Import the LCD library
#include <Keypad.h> //Import the 4 by 4 Button pad library
int delayTimeA = 500;
int delayTimeB = 2000;
int delayTimeC = 250;
const byte numRows= 4; //number of rows on the keypad
const byte numCols= 4; //number of columns on the keypad
//keymap defines the key pressed according to the row and columns just as appears on the keypad
char keymap[numRows][numCols]= 
{
{'1', '2', '3', 'A'}, 
{'4', '5', '6', 'B'}, 
{'7', '8', '9', 'C'},
{'*', '0', '#', 'D'},
};
//Code that shows the the keypad connections to the arduino terminals
byte rowPins[numRows] = {38,39,40,41}; //Rows 0 to 3
byte colPins[numCols]= {A12,A13,A14,A15}; //Columns 0 to 3
//initializes an instance of the Keypad class
Keypad myKeypad= Keypad(makeKeymap(keymap), rowPins, colPins, numRows, numCols);
//Setup 8-Bit mode with no PWM pinouts
LiquidCrystal lcd(28, 29, 30, 31, 32, 33, 34, 35, 36, 37);
/*Initialize the LCD and
tell it which pins are to
be used for communicating*/
void setup()
{
Serial.begin(9600);
// set up the LCD's number of columns and rows:
lcd.begin(16, 2);
}
//If key is pressed, this key is stored in 'keypressed' variable
//If key is not equal to 'NO_KEY', then this key is printed out
//if count=17, then count is reset back to 0 (this means no key is pressed during the whole keypad scan process
void loop()
{
char keypressed = myKeypad.getKey();
lcd.setCursor(3,0);
lcd.print("Waiting...");
lcd.setCursor(2,1);
lcd.print("For Input...");
if (keypressed != NO_KEY){
  lcd.clear();
  Serial.print(keypressed);
  lcd.print("I am MEGA-BREAD.");
  delay(delayTimeA); //Wait
  lcd.setCursor(0, 1);
  lcd.print ("Pressed Key =");
  delay(delayTimeA); //Wait
  lcd.setCursor(14, 1);
  lcd.print (keypressed);
  delay(delayTimeB); //Wait
  lcd.clear();
}
}

// code stored in the sketch: MEGA_BREAD_LCD_16X2.ino
#include <LiquidCrystal.h> //Import the LCD library
#include <Keypad.h> //Import the 4 by 4 Button pad library
int delayTimeA = 500;
int delayTimeB = 750;
int delayTimeC = 1000;
const byte numRows= 4; //number of rows on the keypad
const byte numCols= 4; //number of columns on the keypad
//keymap defines the key pressed according to the row and columns just as appears on the keypad
char keymap[numRows][numCols]= 
{
{'1', '2', '3', 'A'}, 
{'4', '5', '6', 'B'}, 
{'7', '8', '9', 'C'},
{'*', '0', '#', 'D'},
};
//Code that shows the the keypad connections to the arduino terminals
byte rowPins[numRows] = {38,39,40,41}; //Rows 0 to 3
byte colPins[numCols]= {A12,A13,A14,A15}; //Columns 0 to 3
//initializes an instance of the Keypad class
Keypad myKeypad= Keypad(makeKeymap(keymap), rowPins, colPins, numRows, numCols);
//Setup 8-Bit mode with no PWM pinouts
LiquidCrystal lcd(28, 29, 30, 31, 32, 33, 34, 35, 36, 37);
/*Initialize the LCD and
tell it which pins are to
be used for communicating*/
void setup()
{
Serial.begin(9600);
// set up the LCD's number of columns and rows:
lcd.begin(16, 2);
}
//If key is pressed, this key is stored in 'keypressed' variable
//If key is not equal to 'NO_KEY', then this key is printed out
//if count=17, then count is reset back to 0 (this means no key is pressed during the whole keypad scan process
void loop()
{
char keypressed = myKeypad.getKey();
lcd.clear();
lcd.setCursor(3,0);
lcd.print("Waiting...");
lcd.setCursor(2,1);
lcd.print("For Input..."
if (keypressed != NO_KEY){
  lcd.clear();
  Serial.print(keypressed);
  lcd.print("I am MEGA-BREAD.");
  delay(delayTimeA); //Wait
  lcd.setCursor(0, 1);
  lcd.print ("Pressed Key =");
  delay(delayTimeB); //Wait
  lcd.setCursor(14, 1);
  lcd.print (keypressed);
  delay(delayTimeC); //Wait
}
}
